# Fritzing sketch Smart Water Quality Monitoring System (saved by Fritzing 1.0.6)

parts:
  A1 = tds-sensor-meter-v1.0_1
  U1 = DFRobot SEN0189 [package=THT]
  Water_Level_Sensor1 = Water Level Sensor
  VCC1 = 4 x AAA Battery Mount [internal_resistance=0.1Ω]
  Raspberry_Pi_1 = Raspberry Pi 3 [part_number=RPI-3-V1.2]
  ADC1 = MCP3008 [package=dil16]
  M2 = PH meter with sensor in breadboard [package=THT]
  YF-S201_Flow_Meter1 = YF-S201 Water Flow Meter
  DS1 = DS18B20 1-Wire Temperature Sensor Probe

nets:
  N1: A1.pin1, ADC1.CH1
  GND: A1.pin2, U1.P2_2, VCC1.-, Raspberry_Pi_1.GND, ADC1.DGND, ADC1.AGND, M2.pin3, DS1.GND
  3V3: A1.pin3, Raspberry_Pi_1.3v3, Raspberry_Pi_1.3V3, ADC1.VREF, ADC1.VDD, M2.pin2
  N2: U1.P1_1, YF-S201_Flow_Meter1.SIG
  N3: U1.P1_2, YF-S201_Flow_Meter1.GND
  N4: U1.P1_3, YF-S201_Flow_Meter1.VCC
  N5: U1.P2_1, ADC1.CH2
  VCC: U1.P2_3, Water_Level_Sensor1.VCC, VCC1.+, Raspberry_Pi_1.5V, DS1.VDD
  N6: Water_Level_Sensor1.SIG, Raspberry_Pi_1.GPIO26
  N7: Raspberry_Pi_1.GPIO19, ADC1.Din
  N8: Raspberry_Pi_1.GPIO21, ADC1.Dout
  N9: Raspberry_Pi_1.GPIO7, DS1.DQ
  N10: Raspberry_Pi_1.GPIO24, ADC1.CS/SHDN
  N11: Raspberry_Pi_1.GPIO23, ADC1.CLK
  N12: ADC1.CH0, M2.pin1

custom parts:
  : TDS Meter V1.0 Development Board Water Meter Filter Measuring Water Sensor Module.
  DFRobot SEN0189: Turbidity sensor of DFRobot SEN0189
  Water Level Sensor: A water level sensor. This sensor operates at 3V to 5V. The Sig (signal) pin outputs an analogue signal that is in proportion to the amount of water in contact with the sensor.
  PH meter with sensor in breadboard: DFrobot PH meter (SKU SEN0161)
  YF-S201 Water Flow Meter: The YF-S201 Flow Meter. The input voltage is 5V to 24V (DC).
